# Fritzing sketch Diseño Board control LEDs BT Arduino (saved by Fritzing 0.9.3b)
breadboards: 1

parts:
  Componente1 = Arduino Nano (Rev3.0)
  LED1 = LED - 3mm [color="Red (633nm)" package="3 mm [THT]"]
  LED2 = LED - 3mm [color="Red (633nm)" package="3 mm [THT]"]
  LED3 = LED - 3mm [color="Red (633nm)" package="3 mm [THT]"]
  Componente2 = Bluetooth HC-06
  R1 = Resistor [tolerance=±5% resistance=220 package="0603 [SMD]"]
  R2 = Resistor [tolerance=±5% resistance=220 package="0603 [SMD]"]
  R3 = Resistor [tolerance=±5% resistance=220 package="0603 [SMD]"]

nets:
  GND: Componente1.GND, Componente2.GND, R1.Pin_1, R2.Pin_1, R3.Pin_1
  N1: Componente1.D2, Componente2.TXD
  N2: Componente1.D3, Componente2.RXD
  N3: Componente1.D4, LED1.anode
  N4: Componente1.D5, LED2.anode
  N5: Componente1.D6, LED3.anode
  5V: Componente1.5V, Componente2.VCC
  N6: LED1.cathode, R1.Pin_0
  N7: LED2.cathode, R2.Pin_0
  N8: LED3.cathode, R3.Pin_0
